# Fritzing sketch Sous_vide_slow_cooker_controller (saved by Fritzing 0.9.3b)
circuit board: 8.46667cm x 5.64444cm
breadboards: 1

parts:
  Part1 = Arduino Nano (Rev3.0)
  DS1 = DS18B20 1-Wire Temperature Sensor [part_number=DS18B20]
  LCD2 = LCD screen  # not connected
  Grove2 = Grove OLED 128x96

nets:
  N1: Part1.D5, DS1.DQ
  5V: Part1.5V, DS1.VDD, Grove2.VCC
  N2: Part1.A5, Grove2.SCL
  N3: Part1.A4, Grove2.SDA
  GND: DS1.GND, Grove2.GND

notes:
  20x4 LCD Display
  and serial controller

custom parts:
  LCD screen: A standard character display, usually with 2x16 characters. Comes in many colors.
